# Fritzing sketch datacollector (saved by Fritzing 0.6.3b)
breadboards: 2

parts:
  Arduino1 = Arduino
  R1 = Photocell (LDR) [package=THT]
  C1 = Ceramic Capacitor [capacitance=100nF package="100 mil [THT, multilayer]"]
  R2 = Resistor [tolerance=±5% resistance=4.7k package=THT]
  R3 = Resistor [tolerance=±5% resistance=4.7k package=THT]
  R4 = Resistor [tolerance=±5% resistance=4.7k package=THT]
  R5 = Resistor [tolerance=±5% resistance=4.7k package=THT]
  U1 = XBee

nets:
  GND: Arduino1.GND, Arduino1.A0, C1.0, R3.Pin_1, U1.GND
  N1: Arduino1.D3, U1.pin2
  N2: Arduino1.D2, U1.pin3
  +5V: Arduino1.+5V, R1.pin_1, R4.Pin_0, U1.VCC
  N3: Arduino1.A1, R1.pin_0, R2.Pin_0
  N4: C1.1, R5.Pin_0
  N5: R2.Pin_1, R3.Pin_0
  N6: R4.Pin_1, R5.Pin_1
