# Fritzing sketch pr (saved by Fritzing 0.6.3b)
breadboards: 1

parts:
  R1 = Photocell (LDR) [package=THT]
  R2 = Resistor [tolerance=±5% resistance=4.7k package=THT]
  R3 = Resistor [tolerance=±5% resistance=4.7k package=THT]
  Arduino1 = Arduino

nets:
  N1: R1.pin_0, R2.Pin_0, R3.Pin_1, Arduino1.+5V, Arduino1.A1
  N2: R1.pin_1, Arduino1.GND
  N3: R2.Pin_1, R3.Pin_0
